# Fritzing sketch Amplifier (saved by Fritzing 0.9.5d)
breadboards: 1

parts:
  Q1 = NPN-Transistor [package="TO92 [THT]"]
  Q3 = NPN-Transistor [package="TO92 [THT]"]
  C1 = Electrolytic Capacitor [capacitance=100µF package="100 mil [THT, electrolytic]"]
  R2 = Resistor [tolerance=±20% resistance=100 package=THT]
  R3 = Resistor [tolerance=±5% resistance=330 package=THT]
  C2 = Electrolytic Capacitor [capacitance=220µF package="100 mil [THT, electrolytic]"]
  R4 = Resistor [tolerance=±5% resistance=22 package=THT]
  C3 = Electrolytic Capacitor [capacitance=1µF package="100 mil [THT, electrolytic]"]
  R1 = Resistor [tolerance=±5% resistance=100k package="2512 [SMD]"]
  D1 = Rectifier Diode [part_number=1N4001 package="300 mil [THT]"]
  D2 = Rectifier Diode [part_number=1N4001 package="300 mil [THT]"]
  Q2 = PNP-Transistor [package="TO92 [THT]"]

nets:
  N1: Q1.E, Q2.E
  N2: Q1.B, R3.Pin_0, D1.anode
  N3: Q1.C, C1.+, R2.Pin_0, R2.Pin_1, R3.Pin_1, C2.+, R4.Pin_0
  GND: Q3.E, C2.-, Q2.C
  N4: Q3.B, C3.+, R1.Pin_0
  N5: Q3.C, D2.cathode, Q2.B
  N6: C1.-, R1.Pin_1
  5V: R4.Pin_1
  N7: D1.cathode, D2.anode
